# Fritzing sketch Schematics (saved by Fritzing 0.9.3b)
breadboards: 1

parts:
  Argon1 = Particle Argon
  R1 = Slide Potentiometer [maximum_resistance=100kΩ]
  Part1 = Motor Driver 1A Dual TB6612FNG
  M1 = DC Motor
  V5 = DC Power [voltage=10]
  M2 = DC Motor

nets:
  3.3V: Argon1.3.3V, R1.leg2, Part1.VCC
  GND: Argon1.GND, R1.leg1, Part1.GND, V5.V-
  N1: Argon1.A1, R1.wiper
  N2: Argon1.SDA, Part1.AIN1
  N3: Argon1.SCL, Part1.AIN2
  N4: Argon1.D2, Part1.BIN1
  N5: Argon1.D3, Part1.BIN2
  N6: Argon1.D4, Part1.STBY
  N7: Argon1.D7, Part1.PWMA
  N8: Argon1.D8, Part1.PWMB
  N9: Part1.B01, M2.pin_2
  N10: Part1.B02, M2.pin_1
  N11: Part1.A02, M1.pin_1
  N12: Part1.A01, M1.pin_2
  10V: Part1.VM, V5.V+

custom parts:
  Particle Argon: The Argon is a powerful Wi-Fi enabled development board that can act as either a standalone Wi-Fi endpoint or Wi-Fi enabled gateway for Particle Mesh networks. It is based on the Nordic nRF52840 and has built-in battery charging circuitry so it’s easy to connect a Li-Po and deploy your local network in minutes. The Argon is great for connecting existing projects to the Particle Device Cloud or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
